# Fritzing sketch servo (saved by Fritzing 0.9.0b)
breadboards: 1

parts:
  Part1 = Spark Core (v1.0)
  VCC1 = 4 x AAA Battery Mount
  J1 = Basic Servo

nets:
  N1: Part1.A7, J1.pulse
  GND: Part1.GND, VCC1.-, J1.gnd
  VIN: Part1.VIN, VCC1.+, J1.vcc
